# Fritzing sketch Drone-Schematic (saved by Fritzing 0.9.3b)
breadboards: 1

parts:
  Q1 = NPN-Transistor [package="TO92 [THT]"]
  R1 = Resistor [tolerance=±5% resistance=6.5 package=THT]
  R2 = Resistor [tolerance=±5% resistance=47 package=THT]
  Bauteil1 = Arduino Pro Mini v13
  U1 = LIPO-110mAh [package=lipo-110]
  Q2 = NPN-Transistor [package="TO92 [THT]"]
  R3 = Resistor [tolerance=±5% resistance=6.5 package=THT]
  R4 = Resistor [tolerance=±5% resistance=47 package=THT]
  Q3 = NPN-Transistor [package="TO92 [THT]"]
  R5 = Resistor [tolerance=±5% resistance=6.5 package=THT]
  R6 = Resistor [tolerance=±5% resistance=47 package=THT]
  Q4 = NPN-Transistor [package="TO92 [THT]"]
  R7 = Resistor [tolerance=±5% resistance=6.5 package=THT]
  R8 = Resistor [tolerance=±5% resistance=47 package=THT]
  C1 = Electrolytic Capacitor [capacitance=10µF package="100 mil [THT, electrolytic]"]
  C2 = Electrolytic Capacitor [capacitance=10µF package="100 mil [THT, electrolytic]"]
  C3 = Electrolytic Capacitor [capacitance=10µF package="100 mil [THT, electrolytic]"]
  C4 = Electrolytic Capacitor [capacitance=10µF package="100 mil [THT, electrolytic]"]
  C5 = Electrolytic Capacitor [capacitance=220µF package="100 mil [THT, electrolytic]"]
  3-Axis_Accelerometer1 = 3-Axis Accelerometer Breakout - MMA8452Q

nets:
  N1: Q1.E, R1.Pin_1, Bauteil1.A1, C1.+
  N2: Q1.B, R2.Pin_1
  N3: Q1.C, U1.+, Q2.C, Q3.C, Q4.C, C5.+
  N4: R1.Pin_0, U1.-, R3.Pin_0, R5.Pin_0, R7.Pin_0, C1.-, C2.-, C3.-, C4.-, C5.-
  N5: R2.Pin_0, Bauteil1.D6_PWM
  N6: Bauteil1.A4, 3-Axis_Accelerometer1.SDA
  N7: Bauteil1.A5, 3-Axis_Accelerometer1.SCL
  N8: Bauteil1.A3, Q4.E, R7.Pin_1, C4.+
  N9: Bauteil1.A2, Q3.E, R5.Pin_1, C3.+
  N10: Bauteil1.A0, Q2.E, R3.Pin_1, C2.+
  N11: Bauteil1.D9_PWM, R6.Pin_0
  N12: Bauteil1.D5_PWM, R8.Pin_0
  N13: Bauteil1.D3_PWM, R4.Pin_0
  N14: Q2.B, R4.Pin_1
  N15: Q3.B, R6.Pin_1
  N16: Q4.B, R8.Pin_1
